// Logisim project rv32i.circ as structural Verilog
module main (
);

  wire alu_1_zero, and_1_out, clock_1_out, ex_mem_1_branch_ou, ex_mem_1_mem_read, ex_mem_1_mem_write,
       ex_mem_1_zero_out, id_ex_1_alu_src_out, mem_wb_1_mem_to_reg, mem_wb_1_reg_write, Reset_out;
  wire [1:0] control_1_memtoreg, ex_mem_1_wb_out, id_ex_1_alu_op_out, id_ex_1_wb_out;
  wire [2:0] alu_control_1_aluctrl_o, control_1_alusrc, control_1_branch, id_ex_1_m_out;
  wire [3:0] id_ex_1_alu_control_out;
  wire [4:0] ex_mem_1_write_reg_out, id_ex_1_write_reg_out, mem_wb_1_write_reg_out;
  wire [19:0] immgen_1_imm;
  wire [23:0] add_1_s_o, add_2_s_o, ex_mem_1_adress_out, id_ex_1_address_out, id_ex_1_imm_out,
       if_id_1_instruction_address_out, mux_2_1_24b_1_output_0, pc_1_pc_out;
  wire [31:0] alu_1_saida, datamem_subcircuit_1_output_data, ex_mem_1_alu_out, ex_mem_1_write_data_out,
       id_ex_1_imm_32b_out, id_ex_1_reg_file_data_1_out, id_ex_1_reg_file_data_2_out,
       if_id_1_instruction_data_out, im_1_instruction_out, mem_wb_1_alu_res_out, mem_wb_1_datamem_out,
       mux_2_1_1_output_0, mux_2_1_2_output_0, reg_file_1_read_data_1, reg_file_1_read_data_2;

  Clock clock_1 (.out(clock_1_out));
  Button Reset (.out(Reset_out));
  PC pc_1 (.CLK(clock_1_out), .CLR(Reset_out), .PC_IN(mux_2_1_24b_1_output_0), .PC_OUT(pc_1_pc_out));
  IM im_1 (.address(pc_1_pc_out), .clock(clock_1_out), .instruction_out(im_1_instruction_out));
  mux_2_1_24b mux_2_1_24b_1 (
    .selection(and_1_out), .input_0(add_1_s_o), .input_1(ex_mem_1_adress_out),
    .output_0(mux_2_1_24b_1_output_0));
  ADD add_1 (.A_i(pc_1_pc_out), .B_i(24'h4), .S_o(add_1_s_o));
  IF_ID if_id_1 (
    .clock(clock_1_out), .clear(Reset_out), .instruction_address_in(mux_2_1_24b_1_output_0),
    .instruction_data_in(im_1_instruction_out), .instruction_address_out(if_id_1_instruction_address_out),
    .instruction_data_out(if_id_1_instruction_data_out));
  Control control_1 (
    .I(if_id_1_instruction_data_out[6:0]), .ALUSrc(control_1_alusrc[0]), .MemtoReg(control_1_memtoreg[0]),
    .RegWrite(control_1_memtoreg[1]), .MemRead(control_1_branch[1]), .MemWrite(control_1_branch[2]),
    .Branch(control_1_branch[0]), .ALUOp1(control_1_alusrc[1]), .ALUOp0(control_1_alusrc[2]));
  Reg_File reg_file_1 (
    .read_register_1(if_id_1_instruction_data_out[19:15]),
    .read_register_2(if_id_1_instruction_data_out[24:20]), .clock(clock_1_out),
    .write_data(mux_2_1_2_output_0), .clear(Reset_out), .write_control(mem_wb_1_reg_write),
    .write_register(mem_wb_1_write_reg_out), .read_data_1(reg_file_1_read_data_1),
    .read_data_2(reg_file_1_read_data_2));
  ImmGen immgen_1 (.I(if_id_1_instruction_data_out), .Imm(immgen_1_imm));
  ID_EX id_ex_1 (
    .CLK(clock_1_out), .CLR(Reset_out), .WB_IN(control_1_memtoreg), .M_IN(control_1_branch),
    .EX_IN(control_1_alusrc), .ADDRESS_IN(if_id_1_instruction_address_out),
    .REG_FILE_DATA_1_IN(reg_file_1_read_data_1), .REG_FILE_DATA_2_IN(reg_file_1_read_data_2),
    .IMM_IN(immgen_1_imm),
    .ALU_CONTROL_IN({if_id_1_instruction_data_out[30], if_id_1_instruction_data_out[14:12]}),
    .WRITE_REG_IN(if_id_1_instruction_data_out[11:7]), .WB_OUT(id_ex_1_wb_out), .M_OUT(id_ex_1_m_out),
    .ALU_SRC_OUT(id_ex_1_alu_src_out), .ALU_OP_OUT(id_ex_1_alu_op_out), .ADDRESS_OUT(id_ex_1_address_out),
    .REG_FILE_DATA_1_OUT(id_ex_1_reg_file_data_1_out), .REG_FILE_DATA_2_OUT(id_ex_1_reg_file_data_2_out),
    .IMM_32B_OUT(id_ex_1_imm_32b_out), .IMM_OUT(id_ex_1_imm_out), .ALU_CONTROL_OUT(id_ex_1_alu_control_out),
    .WRITE_REG_OUT(id_ex_1_write_reg_out));
  mux_2_1 mux_2_1_1 (
    .selection(id_ex_1_alu_src_out), .input_0(id_ex_1_reg_file_data_2_out), .input_1(id_ex_1_imm_32b_out),
    .output_0(mux_2_1_1_output_0));
  ADD add_2 (.A_i(id_ex_1_address_out), .B_i(id_ex_1_imm_out), .S_o(add_2_s_o));
  ALU alu_1 (
    .input0(id_ex_1_reg_file_data_1_out), .input1(mux_2_1_1_output_0), .operation(alu_control_1_aluctrl_o),
    .zero(alu_1_zero), .saida(alu_1_saida));
  alu_control alu_control_1 (
    .I(id_ex_1_alu_control_out), .ALUop_in(id_ex_1_alu_op_out), .ALUCtrl_o(alu_control_1_aluctrl_o));
  EX_MEM ex_mem_1 (
    .clock(clock_1_out), .clear(Reset_out), .WB_IN(id_ex_1_wb_out), .M_IN(id_ex_1_m_out),
    .ADRESS_IN(add_2_s_o), .ZERO_IN(alu_1_zero), .ALU_IN(alu_1_saida),
    .WRITE_DATA_IN(id_ex_1_reg_file_data_2_out), .WRITE_REG_IN(id_ex_1_write_reg_out),
    .WB_OUT(ex_mem_1_wb_out), .BRANCH_OU(ex_mem_1_branch_ou), .MEM_READ(ex_mem_1_mem_read),
    .MEM_WRITE(ex_mem_1_mem_write), .ADRESS_OUT(ex_mem_1_adress_out), .ZERO_OUT(ex_mem_1_zero_out),
    .ALU_OUT(ex_mem_1_alu_out), .WRITE_DATA_OUT(ex_mem_1_write_data_out),
    .WRITE_REG_OUT(ex_mem_1_write_reg_out));
  and and_1 (and_1_out, ex_mem_1_zero_out, ex_mem_1_branch_ou);
  datamem_subcircuit datamem_subcircuit_1 (
    .input_data(ex_mem_1_write_data_out), .byte_address(ex_mem_1_alu_out), .clock(clock_1_out),
    .read(ex_mem_1_mem_read), .write(ex_mem_1_mem_write), .output_data(datamem_subcircuit_1_output_data));
  MEM_WB mem_wb_1 (
    .CLK(clock_1_out), .CLR(Reset_out), .WB_IN(ex_mem_1_wb_out),
    .DATAMEM_IN(datamem_subcircuit_1_output_data), .ALU_RES_IN(ex_mem_1_alu_out),
    .WRITE_REG_IN(ex_mem_1_write_reg_out), .REG_WRITE(mem_wb_1_reg_write), .MEM_TO_REG(mem_wb_1_mem_to_reg),
    .ALU_RES_OUT(mem_wb_1_alu_res_out), .DATAMEM_OUT(mem_wb_1_datamem_out),
    .WRITE_REG_OUT(mem_wb_1_write_reg_out));
  mux_2_1 mux_2_1_2 (
    .selection(mem_wb_1_mem_to_reg), .input_0(mem_wb_1_alu_res_out), .input_1(mem_wb_1_datamem_out),
    .output_0(mux_2_1_2_output_0));
endmodule

module datamem_subcircuit (
  input  [31:0] input_data,
  input  [31:0] byte_address,
  input  clock,
  input  read,
  input  write,
  output [31:0] output_data
);

  wire [3:0] datamem_interface_1_p16;
  wire [7:0] datamem_interface_1_p6, datamem_interface_1_p7, datamem_interface_1_p8, datamem_interface_1_p9,
       datamem_interface_1_p11, datamem_interface_1_p12, datamem_interface_1_p13, datamem_interface_1_p14;
  wire [15:0] datamem_interface_1_p15;

  // datamem_interface datamem_interface_1: pin names not known; wires that end beside it: input_data, byte_address, clock, read, write, datamem_interface_1_p6, datamem_interface_1_p7, datamem_interface_1_p8, datamem_interface_1_p9, output_data, datamem_interface_1_p11, datamem_interface_1_p12, datamem_interface_1_p13, datamem_interface_1_p14, datamem_interface_1_p15, datamem_interface_1_p16
  datamem datamem_1 (
    .clock(clock), .write_enable(datamem_interface_1_p16[0]), .address(datamem_interface_1_p15),
    .input_data(datamem_interface_1_p11), .output_data(datamem_interface_1_p6));
  datamem datamem_2 (
    .clock(clock), .write_enable(datamem_interface_1_p16[1]), .address(datamem_interface_1_p15),
    .input_data(datamem_interface_1_p12), .output_data(datamem_interface_1_p7));
  datamem datamem_3 (
    .clock(clock), .write_enable(datamem_interface_1_p16[2]), .address(datamem_interface_1_p15),
    .input_data(datamem_interface_1_p13), .output_data(datamem_interface_1_p8));
  datamem datamem_4 (
    .clock(clock), .write_enable(datamem_interface_1_p16[3]), .address(datamem_interface_1_p15),
    .input_data(datamem_interface_1_p14), .output_data(datamem_interface_1_p9));
endmodule

module Reg_File (
  input  [4:0] read_register_1,
  input  [4:0] read_register_2,
  input  clock,
  input  [31:0] write_data,
  input  clear,
  input  write_control,
  input  [4:0] write_register,
  output [31:0] read_data_1,
  output [31:0] read_data_2
);

  wire [31:0] reg32b_falling_edge_1_reg_out, reg32b_falling_edge_2_reg_out, reg32b_falling_edge_3_reg_out,
       reg32b_falling_edge_4_reg_out, reg32b_falling_edge_5_reg_out, reg32b_falling_edge_6_reg_out,
       reg32b_falling_edge_7_reg_out, reg32b_falling_edge_8_reg_out, reg32b_falling_edge_9_reg_out,
       reg32b_falling_edge_10_reg_out, reg32b_falling_edge_11_reg_out, reg32b_falling_edge_12_reg_out,
       reg32b_falling_edge_13_reg_out, reg32b_falling_edge_14_reg_out, reg32b_falling_edge_15_reg_out,
       reg32b_falling_edge_16_reg_out, reg32b_falling_edge_17_reg_out, reg32b_falling_edge_18_reg_out,
       reg32b_falling_edge_19_reg_out, reg32b_falling_edge_20_reg_out, reg32b_falling_edge_21_reg_out,
       reg32b_falling_edge_22_reg_out, reg32b_falling_edge_23_reg_out, reg32b_falling_edge_24_reg_out,
       reg32b_falling_edge_25_reg_out, reg32b_falling_edge_26_reg_out, reg32b_falling_edge_27_reg_out,
       reg32b_falling_edge_28_reg_out, reg32b_falling_edge_29_reg_out, reg32b_falling_edge_30_reg_out,
       reg32b_falling_edge_31_reg_out, reg32b_falling_edge_32_reg_out, register_file_1_load_vector_out;

  register_file register_file_1 (
    .write_address(write_register), .write_control(write_control),
    .load_vector_out(register_file_1_load_vector_out));
  reg32b_falling_edge reg32b_falling_edge_1 (
    .reg_in({32{1'b0}}), .load(1'b1), .clock(clock), .clear(clear), .reg_out(reg32b_falling_edge_1_reg_out));
  reg32b_falling_edge reg32b_falling_edge_2 (
    .reg_in(write_data), .load(register_file_1_load_vector_out[1]), .clock(clock), .clear(clear),
    .reg_out(reg32b_falling_edge_2_reg_out));
  reg32b_falling_edge reg32b_falling_edge_3 (
    .reg_in(write_data), .load(register_file_1_load_vector_out[2]), .clock(clock), .clear(clear),
    .reg_out(reg32b_falling_edge_3_reg_out));
  reg32b_falling_edge reg32b_falling_edge_4 (
    .reg_in(write_data), .load(register_file_1_load_vector_out[3]), .clock(clock), .clear(clear),
    .reg_out(reg32b_falling_edge_4_reg_out));
  reg32b_falling_edge reg32b_falling_edge_5 (
    .reg_in(write_data), .load(register_file_1_load_vector_out[4]), .clock(clock), .clear(clear),
    .reg_out(reg32b_falling_edge_5_reg_out));
  reg32b_falling_edge reg32b_falling_edge_6 (
    .reg_in(write_data), .load(register_file_1_load_vector_out[5]), .clock(clock), .clear(clear),
    .reg_out(reg32b_falling_edge_6_reg_out));
  reg32b_falling_edge reg32b_falling_edge_7 (
    .reg_in(write_data), .load(register_file_1_load_vector_out[6]), .clock(clock), .clear(clear),
    .reg_out(reg32b_falling_edge_7_reg_out));
  reg32b_falling_edge reg32b_falling_edge_8 (
    .reg_in(write_data), .load(register_file_1_load_vector_out[7]), .clock(clock), .clear(clear),
    .reg_out(reg32b_falling_edge_8_reg_out));
  reg32b_falling_edge reg32b_falling_edge_9 (
    .reg_in(write_data), .load(register_file_1_load_vector_out[8]), .clock(clock), .clear(clear),
    .reg_out(reg32b_falling_edge_9_reg_out));
  reg32b_falling_edge reg32b_falling_edge_10 (
    .reg_in(write_data), .load(register_file_1_load_vector_out[9]), .clock(clock), .clear(clear),
    .reg_out(reg32b_falling_edge_10_reg_out));
  reg32b_falling_edge reg32b_falling_edge_11 (
    .reg_in(write_data), .load(register_file_1_load_vector_out[10]), .clock(clock), .clear(clear),
    .reg_out(reg32b_falling_edge_11_reg_out));
  reg32b_falling_edge reg32b_falling_edge_12 (
    .reg_in(write_data), .load(register_file_1_load_vector_out[11]), .clock(clock), .clear(clear),
    .reg_out(reg32b_falling_edge_12_reg_out));
  reg32b_falling_edge reg32b_falling_edge_13 (
    .reg_in(write_data), .load(register_file_1_load_vector_out[12]), .clock(clock), .clear(clear),
    .reg_out(reg32b_falling_edge_13_reg_out));
  reg32b_falling_edge reg32b_falling_edge_14 (
    .reg_in(write_data), .load(register_file_1_load_vector_out[13]), .clock(clock), .clear(clear),
    .reg_out(reg32b_falling_edge_14_reg_out));
  reg32b_falling_edge reg32b_falling_edge_15 (
    .reg_in(write_data), .load(register_file_1_load_vector_out[14]), .clock(clock), .clear(clear),
    .reg_out(reg32b_falling_edge_15_reg_out));
  reg32b_falling_edge reg32b_falling_edge_16 (
    .reg_in(write_data), .load(register_file_1_load_vector_out[15]), .clock(clock), .clear(clear),
    .reg_out(reg32b_falling_edge_16_reg_out));
  reg32b_falling_edge reg32b_falling_edge_17 (
    .reg_in(write_data), .load(register_file_1_load_vector_out[16]), .clock(clock), .clear(clear),
    .reg_out(reg32b_falling_edge_17_reg_out));
  reg32b_falling_edge reg32b_falling_edge_18 (
    .reg_in(write_data), .load(register_file_1_load_vector_out[17]), .clock(clock), .clear(clear),
    .reg_out(reg32b_falling_edge_18_reg_out));
  reg32b_falling_edge reg32b_falling_edge_19 (
    .reg_in(write_data), .load(register_file_1_load_vector_out[18]), .clock(clock), .clear(clear),
    .reg_out(reg32b_falling_edge_19_reg_out));
  reg32b_falling_edge reg32b_falling_edge_20 (
    .reg_in(write_data), .load(register_file_1_load_vector_out[19]), .clock(clock), .clear(clear),
    .reg_out(reg32b_falling_edge_20_reg_out));
  reg32b_falling_edge reg32b_falling_edge_21 (
    .reg_in(write_data), .load(register_file_1_load_vector_out[20]), .clock(clock), .clear(clear),
    .reg_out(reg32b_falling_edge_21_reg_out));
  reg32b_falling_edge reg32b_falling_edge_22 (
    .reg_in(write_data), .load(register_file_1_load_vector_out[21]), .clock(clock), .clear(clear),
    .reg_out(reg32b_falling_edge_22_reg_out));
  reg32b_falling_edge reg32b_falling_edge_23 (
    .reg_in(write_data), .load(register_file_1_load_vector_out[22]), .clock(clock), .clear(clear),
    .reg_out(reg32b_falling_edge_23_reg_out));
  reg32b_falling_edge reg32b_falling_edge_24 (
    .reg_in(write_data), .load(register_file_1_load_vector_out[23]), .clock(clock), .clear(clear),
    .reg_out(reg32b_falling_edge_24_reg_out));
  reg32b_falling_edge reg32b_falling_edge_25 (
    .reg_in(write_data), .load(register_file_1_load_vector_out[24]), .clock(clock), .clear(clear),
    .reg_out(reg32b_falling_edge_25_reg_out));
  reg32b_falling_edge reg32b_falling_edge_26 (
    .reg_in(write_data), .load(register_file_1_load_vector_out[25]), .clock(clock), .clear(clear),
    .reg_out(reg32b_falling_edge_26_reg_out));
  reg32b_falling_edge reg32b_falling_edge_27 (
    .reg_in(write_data), .load(register_file_1_load_vector_out[26]), .clock(clock), .clear(clear),
    .reg_out(reg32b_falling_edge_27_reg_out));
  reg32b_falling_edge reg32b_falling_edge_28 (
    .reg_in(write_data), .load(register_file_1_load_vector_out[27]), .clock(clock), .clear(clear),
    .reg_out(reg32b_falling_edge_28_reg_out));
  reg32b_falling_edge reg32b_falling_edge_29 (
    .reg_in(write_data), .load(register_file_1_load_vector_out[28]), .clock(clock), .clear(clear),
    .reg_out(reg32b_falling_edge_29_reg_out));
  reg32b_falling_edge reg32b_falling_edge_30 (
    .reg_in(write_data), .load(register_file_1_load_vector_out[29]), .clock(clock), .clear(clear),
    .reg_out(reg32b_falling_edge_30_reg_out));
  reg32b_falling_edge reg32b_falling_edge_31 (
    .reg_in(write_data), .load(register_file_1_load_vector_out[30]), .clock(clock), .clear(clear),
    .reg_out(reg32b_falling_edge_31_reg_out));
  reg32b_falling_edge reg32b_falling_edge_32 (
    .reg_in(write_data), .load(register_file_1_load_vector_out[31]), .clock(clock), .clear(clear),
    .reg_out(reg32b_falling_edge_32_reg_out));
  mux_32_1 mux_32_1_1 (
    .selection(read_register_1), .input_0(reg32b_falling_edge_1_reg_out),
    .input_1(reg32b_falling_edge_2_reg_out), .input_2(reg32b_falling_edge_3_reg_out),
    .input_3(reg32b_falling_edge_4_reg_out), .input_4(reg32b_falling_edge_5_reg_out),
    .input_5(reg32b_falling_edge_6_reg_out), .input_6(reg32b_falling_edge_7_reg_out),
    .input_7(reg32b_falling_edge_8_reg_out), .input_8(reg32b_falling_edge_9_reg_out),
    .input_9(reg32b_falling_edge_10_reg_out), .input_10(reg32b_falling_edge_11_reg_out),
    .input_11(reg32b_falling_edge_12_reg_out), .input_12(reg32b_falling_edge_13_reg_out),
    .input_13(reg32b_falling_edge_14_reg_out), .input_14(reg32b_falling_edge_15_reg_out),
    .input_15(reg32b_falling_edge_16_reg_out), .input_16(reg32b_falling_edge_17_reg_out),
    .input_17(reg32b_falling_edge_18_reg_out), .input_18(reg32b_falling_edge_19_reg_out),
    .input_19(reg32b_falling_edge_20_reg_out), .input_20(reg32b_falling_edge_21_reg_out),
    .input_21(reg32b_falling_edge_22_reg_out), .input_22(reg32b_falling_edge_23_reg_out),
    .input_23(reg32b_falling_edge_24_reg_out), .input_24(reg32b_falling_edge_25_reg_out),
    .input_25(reg32b_falling_edge_26_reg_out), .input_26(reg32b_falling_edge_27_reg_out),
    .input_27(reg32b_falling_edge_28_reg_out), .input_28(reg32b_falling_edge_29_reg_out),
    .input_29(reg32b_falling_edge_30_reg_out), .input_30(reg32b_falling_edge_31_reg_out),
    .input_31(reg32b_falling_edge_32_reg_out), .output_0(read_data_1));
  mux_32_1 mux_32_1_2 (
    .selection(read_register_2), .input_0(reg32b_falling_edge_1_reg_out),
    .input_1(reg32b_falling_edge_2_reg_out), .input_2(reg32b_falling_edge_3_reg_out),
    .input_3(reg32b_falling_edge_4_reg_out), .input_4(reg32b_falling_edge_5_reg_out),
    .input_5(reg32b_falling_edge_6_reg_out), .input_6(reg32b_falling_edge_7_reg_out),
    .input_7(reg32b_falling_edge_8_reg_out), .input_8(reg32b_falling_edge_9_reg_out),
    .input_9(reg32b_falling_edge_10_reg_out), .input_10(reg32b_falling_edge_11_reg_out),
    .input_11(reg32b_falling_edge_12_reg_out), .input_12(reg32b_falling_edge_13_reg_out),
    .input_13(reg32b_falling_edge_14_reg_out), .input_14(reg32b_falling_edge_15_reg_out),
    .input_15(reg32b_falling_edge_16_reg_out), .input_16(reg32b_falling_edge_17_reg_out),
    .input_17(reg32b_falling_edge_18_reg_out), .input_18(reg32b_falling_edge_19_reg_out),
    .input_19(reg32b_falling_edge_20_reg_out), .input_20(reg32b_falling_edge_21_reg_out),
    .input_21(reg32b_falling_edge_22_reg_out), .input_22(reg32b_falling_edge_23_reg_out),
    .input_23(reg32b_falling_edge_24_reg_out), .input_24(reg32b_falling_edge_25_reg_out),
    .input_25(reg32b_falling_edge_26_reg_out), .input_26(reg32b_falling_edge_27_reg_out),
    .input_27(reg32b_falling_edge_28_reg_out), .input_28(reg32b_falling_edge_29_reg_out),
    .input_29(reg32b_falling_edge_30_reg_out), .input_30(reg32b_falling_edge_31_reg_out),
    .input_31(reg32b_falling_edge_32_reg_out), .output_0(read_data_2));
endmodule

module IF_ID (
  input  clock,
  input  clear,
  input  [23:0] instruction_address_in,
  input  [31:0] instruction_data_in,
  output [23:0] instruction_address_out,
  output [31:0] instruction_data_out
);

  reg24b reg24b_1 (
    .reg_in(instruction_address_in), .load(1'b1), .clock(clock), .clear(clear),
    .reg_out(instruction_address_out));
  reg32b reg32b_1 (
    .reg_in(instruction_data_in), .load(1'b1), .clock(clock), .clear(clear), .reg_out(instruction_data_out));
endmodule

module ID_EX (
  input  CLK,
  input  CLR,
  input  [1:0] WB_IN,
  input  [2:0] M_IN,
  input  [2:0] EX_IN,
  input  [23:0] ADDRESS_IN,
  input  [31:0] REG_FILE_DATA_1_IN,
  input  [31:0] REG_FILE_DATA_2_IN,
  input  [19:0] IMM_IN,
  input  [3:0] ALU_CONTROL_IN,
  input  [4:0] WRITE_REG_IN,
  output [1:0] WB_OUT,
  output [2:0] M_OUT,
  output ALU_SRC_OUT,
  output [1:0] ALU_OP_OUT,
  output [23:0] ADDRESS_OUT,
  output [31:0] REG_FILE_DATA_1_OUT,
  output [31:0] REG_FILE_DATA_2_OUT,
  output [31:0] IMM_32B_OUT,
  output [23:0] IMM_OUT,
  output [3:0] ALU_CONTROL_OUT,
  output [4:0] WRITE_REG_OUT
);

  reg2b reg2b_1 (.reg_in(WB_IN), .load(1'b1), .clock(CLK), .clear(CLR), .reg_out(WB_OUT));
  reg3b reg3b_1 (.reg_in(M_IN), .load(1'b1), .clock(CLK), .clear(CLR), .reg_out(M_OUT));
  reg3b reg3b_2 (.reg_in(EX_IN), .load(1'b1), .clock(CLK), .clear(CLR), .reg_out({ALU_OP_OUT, ALU_SRC_OUT}));
  reg24b reg24b_1 (.reg_in(ADDRESS_IN), .load(1'b1), .clock(CLK), .clear(CLR), .reg_out(ADDRESS_OUT));
  reg32b reg32b_1 (.reg_in(REG_FILE_DATA_1_IN), .load(1'b1), .clock(CLK), .clear(CLR), .reg_out(REG_FILE_DATA_1_OUT));
  reg32b reg32b_2 (.reg_in(REG_FILE_DATA_2_IN), .load(1'b1), .clock(CLK), .clear(CLR), .reg_out(REG_FILE_DATA_2_OUT));
  reg24b reg24b_2 (.reg_in({4'b0000, IMM_IN}), .load(1'b1), .clock(CLK), .clear(CLR), .reg_out(IMM_32B_OUT[23:0]));
  reg4b reg4b_1 (.reg_in(ALU_CONTROL_IN), .load(1'b1), .clock(CLK), .clear(CLR), .reg_out(ALU_CONTROL_OUT));
  reg5b reg5b_1 (.reg_in(WRITE_REG_IN), .load(1'b1), .clock(CLK), .clear(CLR), .reg_out(WRITE_REG_OUT));

  assign IMM_32B_OUT[31:24] = {8{1'b0}};
  assign IMM_OUT = IMM_32B_OUT[23:0];
endmodule

module EX_MEM (
  input  clock,
  input  clear,
  input  [1:0] WB_IN,
  input  [2:0] M_IN,
  input  [23:0] ADRESS_IN,
  input  ZERO_IN,
  input  [31:0] ALU_IN,
  input  [31:0] WRITE_DATA_IN,
  input  [4:0] WRITE_REG_IN,
  output [1:0] WB_OUT,
  output BRANCH_OU,
  output MEM_READ,
  output MEM_WRITE,
  output [23:0] ADRESS_OUT,
  output ZERO_OUT,
  output [31:0] ALU_OUT,
  output [31:0] WRITE_DATA_OUT,
  output [4:0] WRITE_REG_OUT
);

  reg2b reg2b_1 (.reg_in(WB_IN), .load(1'b1), .clock(clock), .clear(clear), .reg_out(WB_OUT));
  reg3b reg3b_1 (.reg_in(M_IN), .load(1'b1), .clock(clock), .clear(clear), .reg_out({MEM_WRITE, MEM_READ, BRANCH_OU}));
  reg24b reg24b_1 (.reg_in(ADRESS_IN), .load(1'b1), .clock(clock), .clear(clear), .reg_out(ADRESS_OUT));
  reg1b reg1b_1 (.reg_in(ZERO_IN), .load(1'b1), .clock(clock), .clear(clear), .reg_out(ZERO_OUT));
  reg32b reg32b_1 (.reg_in(ALU_IN), .load(1'b1), .clock(clock), .clear(clear), .reg_out(ALU_OUT));
  reg32b reg32b_2 (.reg_in(WRITE_DATA_IN), .load(1'b1), .clock(clock), .clear(clear), .reg_out(WRITE_DATA_OUT));
  reg5b reg5b_1 (.reg_in(WRITE_REG_IN), .load(1'b1), .clock(clock), .clear(clear), .reg_out(WRITE_REG_OUT));
endmodule

module MEM_WB (
  input  CLK,
  input  CLR,
  input  [1:0] WB_IN,
  input  [31:0] DATAMEM_IN,
  input  [31:0] ALU_RES_IN,
  input  [4:0] WRITE_REG_IN,
  output REG_WRITE,
  output MEM_TO_REG,
  output [31:0] ALU_RES_OUT,
  output [31:0] DATAMEM_OUT,
  output [4:0] WRITE_REG_OUT
);

  reg2b reg2b_1 (.reg_in(WB_IN), .load(1'b1), .clock(CLK), .clear(CLR), .reg_out({REG_WRITE, MEM_TO_REG}));
  reg32b reg32b_1 (.reg_in(DATAMEM_IN), .load(1'b1), .clock(CLK), .clear(CLR), .reg_out(DATAMEM_OUT));
  reg32b reg32b_2 (.reg_in(ALU_RES_IN), .load(1'b1), .clock(CLK), .clear(CLR), .reg_out(ALU_RES_OUT));
  reg5b reg5b_1 (.reg_in(WRITE_REG_IN), .load(1'b1), .clock(CLK), .clear(CLR), .reg_out(WRITE_REG_OUT));
endmodule

module IM (
  input  [23:0] address,
  input  clock,
  output [31:0] instruction_out
);

  RAM #(.addrWidth(24), .dataWidth(32)) ram_1 (
    .addr(address), .we(1'b0), .oe(1'b1), .clk(clock), .dout(instruction_out));  // open: din
endmodule

module PC (
  input  CLK,
  input  CLR,
  input  [23:0] PC_IN,
  output [23:0] PC_OUT
);

  reg24b reg24b_1 (.reg_in(PC_IN), .load(1'b1), .clock(CLK), .clear(CLR), .reg_out(PC_OUT));
endmodule

// VHDL entity Control, as the project stores it:
--------------------------------------------------------------------------------
-- Project :
-- File    :
-- Autor   :
-- Date    :
--
--------------------------------------------------------------------------------
-- Description :
--
--------------------------------------------------------------------------------

LIBRARY ieee;
USE ieee.std_logic_1164.all;

ENTITY Control IS
  PORT (
  ------------------------------------------------------------------------------
  --Insert input ports below
    I    : IN  std_logic_vector(6 DOWNTO 0); -- input vector example
  ------------------------------------------------------------------------------
  --Insert output ports below
    ALUSrc        : OUT std_logic;                    -- output bit example
    MemtoReg      : OUT std_logic;  -- output vector example
    RegWrite      : OUT std_logic;
    MemRead	   : OUT std_logic;
    MemWrite      : OUT std_logic;
    Branch        : OUT std_logic;
    ALUOp1	   : OUT std_logic;
    ALUOp0	   : OUT std_logic
    
    );
END Control;

--------------------------------------------------------------------------------
--Complete your VHDL description below
--------------------------------------------------------------------------------

ARCHITECTURE TypeArchitecture OF Control IS

BEGIN

with I select ALUSrc <=
		'0' when "0110011",  --lw e sw (alu add)
		'1' when "0000011",  --beq (alu subtract)
		'1' when "0100011",  --R-format (add)
		'0' when "1100011",  --R-format (sub)
				
		'X' when others;

with I select MemtoReg <=
		'0' when "0110011",  --lw e sw (alu add)
		'1' when "0000011",  --beq (alu subtract)
		'X' when "0100011",  --R-format (add)
		'X' when "1100011",  --R-format (sub)
				
		'X' when others;

with I select RegWrite <=
		'1' when "0110011",  --lw e sw (alu add)
		'1' when "0000011",  --beq (alu subtract)
		'0' when "0100011",  --R-format (add)
		'0' when "1100011",  --R-format (sub)
				
		'X' when others;

with I select MemRead <=
		'0' when "0110011",  --lw e sw (alu add)
		'1' when "0000011",  --beq (alu subtract)
		'0' when "0100011",  --R-format (add)
		'0' when "1100011",  --R-format (sub)
				
		'X' when others;

with I select MemWrite <=
		'0' when "0110011",  --lw e sw (alu add)
		'0' when "0000011",  --beq (alu subtract)
		'1' when "0100011",  --R-format (add)
		'0' when "1100011",  --R-format (sub)
				
		'X' when others;

with I select Branch <=
		'0' when "0110011",  --lw e sw (alu add)
		'0' when "0000011",  --beq (alu subtract)
		'0' when "0100011",  --R-format (add)
		'1' when "1100011",  --R-format (sub)
				
		'X' when others;

with I select ALUOp1 <=
		'1' when "0110011",  --lw e sw (alu add)
		'0' when "0000011",  --beq (alu subtract)
		'0' when "0100011",  --R-format (add)
		'0' when "1100011",  --R-format (sub)
				
		'X' when others;

with I select ALUOp0 <=
		'0' when "0110011",  --lw e sw (alu add)
		'0' when "0000011",  --beq (alu subtract)
		'0' when "0100011",  --R-format (add)
		'1' when "1100011",  --R-format (sub)
				
		'X' when others;


END TypeArchitecture;

// VHDL entity alu_control, as the project stores it:
--------------------------------------------------------------------------------
-- Project :
-- File    :
-- Autor   :
-- Date    :
--
--------------------------------------------------------------------------------
-- Description :
--
--------------------------------------------------------------------------------

LIBRARY ieee;
USE ieee.std_logic_1164.all;

ENTITY alu_control IS
  PORT (
  ------------------------------------------------------------------------------
  --Insert input ports below
    I        : IN  std_logic_vector(3 DOWNTO 0); 
    ALUop_in : IN std_logic_vector(1 downto 0); -- input vector example
  ------------------------------------------------------------------------------
  --Insert output ports below
    ALUCtrl_o        : OUT std_logic_vector(2 downto 0)                   -- output bit example
    );
END alu_control;

--------------------------------------------------------------------------------
--Complete your VHDL description below
--------------------------------------------------------------------------------

ARCHITECTURE TypeArchitecture OF alu_control IS

BEGIN

	with I&ALUop_in select ALUCtrl_o <=
		"000" when "XXXX00",  --lw e sw (alu add)
		"001" when "XXXXX1",  --beq (alu subtract)
		"000" when "00001X",  --R-format (add)
		"001" when "10001X",  --R-format (sub)
		"111" when "01111X",  --R-format (and)
		"110" when "01101X",  --R-format (or)
		
		
		"100" when others;

END TypeArchitecture;

// VHDL entity ImmGen, as the project stores it:
--------------------------------------------------------------------------------
-- Project :
-- File    :
-- Autor   :
-- Date    :
--
--------------------------------------------------------------------------------
-- Description :
--
--------------------------------------------------------------------------------

LIBRARY ieee;
USE ieee.std_logic_1164.all;

ENTITY ImmGen IS
  PORT (
  ------------------------------------------------------------------------------
  --Insert input ports below
    I        : IN  std_logic_vector(31 DOWNTO 0); -- input vector example
  ------------------------------------------------------------------------------
  --Insert output ports below
    Imm        : OUT std_logic_vector(19 downto 0)                   -- output bit example
    );
END ImmGen;

--------------------------------------------------------------------------------
--Complete your VHDL description below
--------------------------------------------------------------------------------

ARCHITECTURE TypeArchitecture OF ImmGen IS

BEGIN

	with I(6 downto 0) select Imm <=
		"00000000"&I(31 downto 20) when "0000011",  --I-type 
		"00000000"&I(31 downto 20) when "0010011",  --I-type
		"00000000"&I(31 downto 20) when "1100111",  --I-type (jalr rd, rs, imm)
		"00000000"&I(31 downto 25)&I(11 downto 7) when "0100011", --S-type (sw rs2, offset(rs1))
		"00000000"&I(31)&I(7)&I(30 downto 25)&I(11 downto 8) when "1100011", --B-type
		I(31 downto 12) when "0110111", --U-type (lui rd, offset)
		I(31)&I(19 downto 12)&I(20)&I(30 downto 21) when "1101111", --J-type (jal rd, imm)
		"XXXXXXXXXXXXXXXXXXXX" when others;

END TypeArchitecture;

// VHDL entity ADD, as the project stores it:
--------------------------------------------------------------------------------
-- Project :
-- File    :
-- Autor   :
-- Date    :
--
--------------------------------------------------------------------------------
-- Description :
--
--------------------------------------------------------------------------------

LIBRARY ieee;
USE ieee.std_logic_1164.all;

ENTITY ADD IS
  PORT (
  ------------------------------------------------------------------------------
  
    A_i      : IN  std_logic_vector(23 DOWNTO 0);        --operando 1               
    B_i        : IN  std_logic_vector(23 DOWNTO 0);      --operando 2
  ------------------------------------------------------------------------------
    S_o        : OUT std_logic_vector(23 DOWNTO 0)  -- Saida
    );
END ADD;

--------------------------------------------------------------------------------
--Complete your VHDL description below
--------------------------------------------------------------------------------

ARCHITECTURE TypeArchitecture OF ADD IS

signal p : std_logic_vector(23 downto 0);
signal g : std_logic_vector(23 downto 0);
signal c : std_logic_vector(23 downto 0);
signal S : std_logic_vector(23 downto 0);


BEGIN

p <= A_i xor B_i;
g <= A_i and B_i;

--estrutura do carry lookahead
c(0) <= '0';
c(1) <= g(0) or 
		 (p(0) and c(0));
				 
c(2) <= g(1) or
		 (p(1) and g(0)) or 	 
		 (p(1) and p(0) and c(0));

c(3) <= g(2) or
		 (p(2) and g(1)) or
		 (p(2) and p(1) and g(0)) or
		 (p(2) and p(1) and p(0) and c(0));
		  
c(4) <= g(3) or 
		 (p(3) and g(2)) or
		 (p(3) and p(2) and g(1)) or		 
		 (p(3) and p(2) and p(1) and g(0)) or
		 (p(3) and p(2) and p(1) and p(0) and c(0)); 
		 
c(5) <= g(4) or 
		 (p(4) and g(3)) or
		 (p(4) and p(3) and g(2)) or
		 (p(4) and p(3) and p(2) and g(1)) or
		 (p(4) and p(3) and p(2) and p(1) and g(0)) or 
		 (p(4) and p(3) and p(2) and p(1) and p(0) and c(0));		 				 

	
c(6) <= g(5) or
		 (p(5) and g(4)) or 
		 (p(5) and p(4) and g(3)) or
		 (p(5) and p(4) and p(3) and g(2)) or
		 (p(5) and p(4) and p(3) and p(2) and g(1)) or
		 (p(5) and p(4) and p(3) and p(2) and p(1) and g(0)) or 
		 (p(5) and p(4) and p(3) and p(2) and p(1) and p(0) and c(0)); 		

c(7) <= g(6) or
		 (p(6) and g(5)) or
		 (p(6) and p(5) and g(4)) or
		 (p(6) and p(5) and p(4) and g(3)) or
		 (p(6) and p(5) and p(4) and p(3) and g(2)) or
		 (p(6) and p(5) and p(4) and p(3) and p(2) and g(1)) or
		 (p(6) and p(5) and p(4) and p(3) and p(2) and p(1) and g(0)) or
		 (p(6) and p(5) and p(4) and p(3) and p(2) and p(1) and p(0) and c(0)); 

c(8) <= g(7) or
		 (p(7) and g(6)) or
		 (p(7) and p(6) and g(5)) or
		 (p(7) and p(6) and p(5) and g(4)) or
		 (p(7) and p(6) and p(5) and p(4) and g(3)) or
		 (p(7) and p(6) and p(5) and p(4) and p(3) and g(2)) or	
		 (p(7) and p(6) and p(5) and p(4) and p(3) and p(2) and g(1)) or
		 (p(7) and p(6) and p(5) and p(4) and p(3) and p(2) and p(1) and g(0)) or 
		 (p(7) and p(6) and p(5) and p(4) and p(3) and p(2) and p(1) and p(0) and c(0));

c(9) <= g(8) or
		 (p(8) and g(7)) or
		 (p(8) and p(7) and g(6)) or
		 (p(8) and p(7) and p(6) and g(5)) or
		 (p(8) and p(7) and p(6) and p(5) and g(4)) or
		 (p(8) and p(7) and p(6) and p(5) and p(4) and g(3)) or	
		 (p(8) and p(7) and p(6) and p(5) and p(4) and p(3) and g(2)) or
		 (p(8) and p(7) and p(6) and p(5) and p(4) and p(3) and p(2) and g(1)) or 
		 (p(8) and p(7) and p(6) and p(5) and p(4) and p(3) and p(2) and p(1) and g(0)) or 
		 (p(8) and p(7) and p(6) and p(5) and p(4) and p(3) and p(2) and p(1) and p(0) and c(0));

c(10) <= g(9) or
		 (p(9) and g(8)) or
		 (p(9) and p(8) and g(7)) or
		 (p(9) and p(8) and p(7) and g(6)) or
		 (p(9) and p(8) and p(7) and p(6) and g(5)) or
		 (p(9) and p(8) and p(7) and p(6) and p(5) and g(4)) or
		 (p(9) and p(8) and p(7) and p(6) and p(5) and p(4) and g(3)) or
		 (p(9) and p(8) and p(7) and p(6) and p(5) and p(4) and p(3) and g(2)) or
		 (p(9) and p(8) and p(7) and p(6) and p(5) and p(4) and p(3) and p(2) and g(1)) or
		 (p(9) and p(8) and p(7) and p(6) and p(5) and p(4) and p(3) and p(2) and p(1) and g(0)) or
		 (p(9) and p(8) and p(7) and p(6) and p(5) and p(4) and p(3) and p(2) and p(1) and p(0) and c(0));


c(11) <= g(10) or
		 (p(10) and g(9)) or
		 (p(10) and p(9) and g(8)) or
		 (p(10) and p(9) and p(8) and g(7)) or
		 (p(10) and p(9) and p(8) and p(7) and g(6)) or
		 (p(10) and p(9) and p(8) and p(7) and p(6) and g(5)) or
		 (p(10) and p(9) and p(8) and p(7) and p(6) and p(5) and g(4)) or
		 (p(10) and p(9) and p(8) and p(7) and p(6) and p(5) and p(4) and g(3)) or
		 (p(10) and p(9) and p(8) and p(7) and p(6) and p(5) and p(4) and p(3) and g(2)) or
		 (p(10) and p(9) and p(8) and p(7) and p(6) and p(5) and p(4) and p(3) and p(2) and g(1)) or
		 (p(10) and p(9) and p(8) and p(7) and p(6) and p(5) and p(4) and p(3) and p(2) and p(1) and g(0)) or
		 (p(10) and p(9) and p(8) and p(7) and p(6) and p(5) and p(4) and p(3) and p(2) and p(1) and p(0) and c(0));
		 
c(12) <= g(11) or
		 (p(11) and g(10)) or
		 (p(11) and p(10) and g(9)) or
		 (p(11) and p(10) and p(9) and g(8)) or
		 (p(11) and p(10) and p(9) and p(8) and g(7)) or
		 (p(11) and p(10) and p(9) and p(8) and p(7) and g(6)) or
		 (p(11) and p(10) and p(9) and p(8) and p(7) and p(6) and g(5)) or
		 (p(11) and p(10) and p(9) and p(8) and p(7) and p(6) and p(5) and g(4)) or
		 (p(11) and p(10) and p(9) and p(8) and p(7) and p(6) and p(5) and p(4) and g(3)) or
		 (p(11) and p(10) and p(9) and p(8) and p(7) and p(6) and p(5) and p(4) and p(3) and g(2)) or
		 (p(11) and p(10) and p(9) and p(8) and p(7) and p(6) and p(5) and p(4) and p(3) and p(2) and g(1)) or
		 (p(11) and p(10) and p(9) and p(8) and p(7) and p(6) and p(5) and p(4) and p(3) and p(2) and p(1) and g(0)) or
		 (p(11) and p(10) and p(9) and p(8) and p(7) and p(6) and p(5) and p(4) and p(3) and p(2) and p(1) and p(0) and c(0));

c(13) <= g(12) or
		 (p(12) and g(11)) or
		 (p(12) and p(11) and g(10)) or
		 (p(12) and p(11) and p(10) and g(9)) or
		 (p(12) and p(11) and p(10) and p(9) and g(8)) or
		 (p(12) and p(11) and p(10) and p(9) and p(8) and g(7)) or
		 (p(12) and p(11) and p(10) and p(9) and p(8) and p(7) and g(6)) or
		 (p(12) and p(11) and p(10) and p(9) and p(8) and p(7) and p(6) and g(5)) or
		 (p(12) and p(11) and p(10) and p(9) and p(8) and p(7) and p(6) and p(5) and g(4)) or
		 (p(12) and p(11) and p(10) and p(9) and p(8) and p(7) and p(6) and p(5) and p(4) and g(3)) or
		 (p(12) and p(11) and p(10) and p(9) and p(8) and p(7) and p(6) and p(5) and p(4) and p(3) and g(2)) or
		 (p(12) and p(11) and p(10) and p(9) and p(8) and p(7) and p(6) and p(5) and p(4) and p(3) and p(2) and g(1)) or
		 (p(12) and p(11) and p(10) and p(9) and p(8) and p(7) and p(6) and p(5) and p(4) and p(3) and p(2) and p(1) and g(0)) or
		 (p(12) and p(11) and p(10) and p(9) and p(8) and p(7) and p(6) and p(5) and p(4) and p(3) and p(2) and p(1) and p(0) and c(0));	

c(14) <= g(13) or
		 (p(13) and g(12)) or
		 (p(13) and p(12) and g(11)) or
		 (p(13) and p(12) and p(11) and g(10)) or
		 (p(13) and p(12) and p(11) and p(10) and g(9)) or
		 (p(13) and p(12) and p(11) and p(10) and p(9) and g(8)) or
		 (p(13) and p(12) and p(11) and p(10) and p(9) and p(8) and g(7)) or
		 (p(13) and p(12) and p(11) and p(10) and p(9) and p(8) and p(7) and g(6)) or
		 (p(13) and p(12) and p(11) and p(10) and p(9) and p(8) and p(7) and p(6) and g(5)) or
		 (p(13) and p(12) and p(11) and p(10) and p(9) and p(8) and p(7) and p(6) and p(5) and g(4)) or
		 (p(13) and p(12) and p(11) and p(10) and p(9) and p(8) and p(7) and p(6) and p(5) and p(4) and g(3)) or
		 (p(13) and p(12) and p(11) and p(10) and p(9) and p(8) and p(7) and p(6) and p(5) and p(4) and p(3) and g(2)) or
		 (p(13) and p(12) and p(11) and p(10) and p(9) and p(8) and p(7) and p(6) and p(5) and p(4) and p(3) and p(2) and g(1)) or
		 (p(13) and p(12) and p(11) and p(10) and p(9) and p(8) and p(7) and p(6) and p(5) and p(4) and p(3) and p(2) and p(1) and g(0)) or
		 (p(13) and p(12) and p(11) and p(10) and p(9) and p(8) and p(7) and p(6) and p(5) and p(4) and p(3) and p(2) and p(1) and p(0) and c(0));

c(15) <= g(14) or
		 (p(14) and g(13)) or
		 (p(14) and p(13) and g(12)) or
		 (p(14) and p(13) and p(12) and g(11)) or
		 (p(14) and p(13) and p(12) and p(11) and g(10)) or
		 (p(14) and p(13) and p(12) and p(11) and p(10) and g(9)) or
		 (p(14) and p(13) and p(12) and p(11) and p(10) and p(9) and g(8)) or
		 (p(14) and p(13) and p(12) and p(11) and p(10) and p(9) and p(8) and g(7)) or
		 (p(14) and p(13) and p(12) and p(11) and p(10) and p(9) and p(8) and p(7) and g(6)) or
		 (p(14) and p(13) and p(12) and p(11) and p(10) and p(9) and p(8) and p(7) and p(6) and g(5)) or
		 (p(14) and p(13) and p(12) and p(11) and p(10) and p(9) and p(8) and p(7) and p(6) and p(5) and g(4)) or
		 (p(14) and p(13) and p(12) and p(11) and p(10) and p(9) and p(8) and p(7) and p(6) and p(5) and p(4) and g(3)) or
		 (p(14) and p(13) and p(12) and p(11) and p(10) and p(9) and p(8) and p(7) and p(6) and p(5) and p(4) and p(3) and g(2)) or
		 (p(14) and p(13) and p(12) and p(11) and p(10) and p(9) and p(8) and p(7) and p(6) and p(5) and p(4) and p(3) and p(2) and g(1)) or
		 (p(14) and p(13) and p(12) and p(11) and p(10) and p(9) and p(8) and p(7) and p(6) and p(5) and p(4) and p(3) and p(2) and p(1) and g(0)) or
		 (p(14) and p(13) and p(12) and p(11) and p(10) and p(9) and p(8) and p(7) and p(6) and p(5) and p(4) and p(3) and p(2) and p(1) and p(0) and c(0));

c(16) <= g(15) or
		 (p(15) and g(14)) or
		 (p(15) and p(14) and g(13)) or
		 (p(15) and p(14) and p(13) and g(12)) or
		 (p(15) and p(14) and p(13) and p(12) and g(11)) or
		 (p(15) and p(14) and p(13) and p(12) and p(11) and g(10)) or
		 (p(15) and p(14) and p(13) and p(12) and p(11) and p(10) and g(9)) or
		 (p(15) and p(14) and p(13) and p(12) and p(11) and p(10) and p(9) and g(8)) or
		 (p(15) and p(14) and p(13) and p(12) and p(11) and p(10) and p(9) and p(8) and g(7)) or
		 (p(15) and p(14) and p(13) and p(12) and p(11) and p(10) and p(9) and p(8) and p(7) and g(6)) or
		 (p(15) and p(14) and p(13) and p(12) and p(11) and p(10) and p(9) and p(8) and p(7) and p(6) and g(5)) or
		 (p(15) and p(14) and p(13) and p(12) and p(11) and p(10) and p(9) and p(8) and p(7) and p(6) and p(5) and g(4)) or
		 (p(15) and p(14) and p(13) and p(12) and p(11) and p(10) and p(9) and p(8) and p(7) and p(6) and p(5) and p(4) and g(3)) or
		 (p(15) and p(14) and p(13) and p(12) and p(11) and p(10) and p(9) and p(8) and p(7) and p(6) and p(5) and p(4) and p(3) and g(2)) or
		 (p(15) and p(14) and p(13) and p(12) and p(11) and p(10) and p(9) and p(8) and p(7) and p(6) and p(5) and p(4) and p(3) and p(2) and g(1)) or
		 (p(15) and p(14) and p(13) and p(12) and p(11) and p(10) and p(9) and p(8) and p(7) and p(6) and p(5) and p(4) and p(3) and p(2) and p(1) and g(0)) or
		 (p(15) and p(14) and p(13) and p(12) and p(11) and p(10) and p(9) and p(8) and p(7) and p(6) and p(5) and p(4) and p(3) and p(2) and p(1) and p(0) and c(0));

c(17) <= g(16) or
		 (p(16) and g(15)) or
		 (p(16) and p(15) and g(14)) or
		 (p(16) and p(15) and p(14) and g(13)) or
		 (p(16) and p(15) and p(14) and p(13) and g(12)) or
		 (p(16) and p(15) and p(14) and p(13) and p(12) and g(11)) or
		 (p(16) and p(15) and p(14) and p(13) and p(12) and p(11) and g(10)) or
		 (p(16) and p(15) and p(14) and p(13) and p(12) and p(11) and p(10) and g(9)) or
		 (p(16) and p(15) and p(14) and p(13) and p(12) and p(11) and p(10) and p(9) and g(8)) or
		 (p(16) and p(15) and p(14) and p(13) and p(12) and p(11) and p(10) and p(9) and p(8) and g(7)) or
		 (p(16) and p(15) and p(14) and p(13) and p(12) and p(11) and p(10) and p(9) and p(8) and p(7) and g(6)) or
		 (p(16) and p(15) and p(14) and p(13) and p(12) and p(11) and p(10) and p(9) and p(8) and p(7) and p(6) and g(5)) or
		 (p(16) and p(15) and p(14) and p(13) and p(12) and p(11) and p(10) and p(9) and p(8) and p(7) and p(6) and p(5) and g(4)) or
		 (p(16) and p(15) and p(14) and p(13) and p(12) and p(11) and p(10) and p(9) and p(8) and p(7) and p(6) and p(5) and p(4) and g(3)) or
		 (p(16) and p(15) and p(14) and p(13) and p(12) and p(11) and p(10) and p(9) and p(8) and p(7) and p(6) and p(5) and p(4) and p(3) and g(2)) or
		 (p(16) and p(15) and p(14) and p(13) and p(12) and p(11) and p(10) and p(9) and p(8) and p(7) and p(6) and p(5) and p(4) and p(3) and p(2) and g(1)) or
		 (p(16) and p(15) and p(14) and p(13) and p(12) and p(11) and p(10) and p(9) and p(8) and p(7) and p(6) and p(5) and p(4) and p(3) and p(2) and p(1) and g(0)) or
		 (p(16) and p(15) and p(14) and p(13) and p(12) and p(11) and p(10) and p(9) and p(8) and p(7) and p(6) and p(5) and p(4) and p(3) and p(2) and p(1) and p(0) and c(0));

c(18) <= g(17) or
		 (p(17) and g(16)) or
		 (p(17) and p(16) and g(15)) or
		 (p(17) and p(16) and p(15) and g(14)) or
		 (p(17) and p(16) and p(15) and p(14) and g(13)) or
		 (p(17) and p(16) and p(15) and p(14) and p(13) and g(12)) or
		 (p(17) and p(16) and p(15) and p(14) and p(13) and p(12) and g(11)) or
		 (p(17) and p(16) and p(15) and p(14) and p(13) and p(12) and p(11) and g(10)) or
		 (p(17) and p(16) and p(15) and p(14) and p(13) and p(12) and p(11) and p(10) and g(9)) or
		 (p(17) and p(16) and p(15) and p(14) and p(13) and p(12) and p(11) and p(10) and p(9) and g(8)) or
		 (p(17) and p(16) and p(15) and p(14) and p(13) and p(12) and p(11) and p(10) and p(9) and p(8) and g(7)) or
		 (p(17) and p(16) and p(15) and p(14) and p(13) and p(12) and p(11) and p(10) and p(9) and p(8) and p(7) and g(6)) or
		 (p(17) and p(16) and p(15) and p(14) and p(13) and p(12) and p(11) and p(10) and p(9) and p(8) and p(7) and p(6) and g(5)) or
		 (p(17) and p(16) and p(15) and p(14) and p(13) and p(12) and p(11) and p(10) and p(9) and p(8) and p(7) and p(6) and p(5) and g(4)) or
		 (p(17) and p(16) and p(15) and p(14) and p(13) and p(12) and p(11) and p(10) and p(9) and p(8) and p(7) and p(6) and p(5) and p(4) and g(3)) or
		 (p(17) and p(16) and p(15) and p(14) and p(13) and p(12) and p(11) and p(10) and p(9) and p(8) and p(7) and p(6) and p(5) and p(4) and p(3) and g(2)) or
		 (p(17) and p(16) and p(15) and p(14) and p(13) and p(12) and p(11) and p(10) and p(9) and p(8) and p(7) and p(6) and p(5) and p(4) and p(3) and p(2) and g(1)) or
		 (p(17) and p(16) and p(15) and p(14) and p(13) and p(12) and p(11) and p(10) and p(9) and p(8) and p(7) and p(6) and p(5) and p(4) and p(3) and p(2) and p(1) and g(0)) or
		 (p(17) and p(16) and p(15) and p(14) and p(13) and p(12) and p(11) and p(10) and p(9) and p(8) and p(7) and p(6) and p(5) and p(4) and p(3) and p(2) and p(1) and p(0) and c(0));	

c(19) <= g(18) or
		 (p(18) and g(17)) or
		 (p(18) and p(17) and g(16)) or
		 (p(18) and p(17) and p(16) and g(15)) or
		 (p(18) and p(17) and p(16) and p(15) and g(14)) or
		 (p(18) and p(17) and p(16) and p(15) and p(14) and g(13)) or
		 (p(18) and p(17) and p(16) and p(15) and p(14) and p(13) and g(12)) or
		 (p(18) and p(17) and p(16) and p(15) and p(14) and p(13) and p(12) and g(11)) or
		 (p(18) and p(17) and p(16) and p(15) and p(14) and p(13) and p(12) and p(11) and g(10)) or
		 (p(18) and p(17) and p(16) and p(15) and p(14) and p(13) and p(12) and p(11) and p(10) and g(9)) or
		 (p(18) and p(17) and p(16) and p(15) and p(14) and p(13) and p(12) and p(11) and p(10) and p(9) and g(8)) or
		 (p(18) and p(17) and p(16) and p(15) and p(14) and p(13) and p(12) and p(11) and p(10) and p(9) and p(8) and g(7)) or
		 (p(18) and p(17) and p(16) and p(15) and p(14) and p(13) and p(12) and p(11) and p(10) and p(9) and p(8) and p(7) and g(6)) or
		 (p(18) and p(17) and p(16) and p(15) and p(14) and p(13) and p(12) and p(11) and p(10) and p(9) and p(8) and p(7) and p(6) and g(5)) or
		 (p(18) and p(17) and p(16) and p(15) and p(14) and p(13) and p(12) and p(11) and p(10) and p(9) and p(8) and p(7) and p(6) and p(5) and g(4)) or
		 (p(18) and p(17) and p(16) and p(15) and p(14) and p(13) and p(12) and p(11) and p(10) and p(9) and p(8) and p(7) and p(6) and p(5) and p(4) and g(3)) or
		 (p(18) and p(17) and p(16) and p(15) and p(14) and p(13) and p(12) and p(11) and p(10) and p(9) and p(8) and p(7) and p(6) and p(5) and p(4) and p(3) and g(2)) or
		 (p(18) and p(17) and p(16) and p(15) and p(14) and p(13) and p(12) and p(11) and p(10) and p(9) and p(8) and p(7) and p(6) and p(5) and p(4) and p(3) and p(2) and g(1)) or
		 (p(18) and p(17) and p(16) and p(15) and p(14) and p(13) and p(12) and p(11) and p(10) and p(9) and p(8) and p(7) and p(6) and p(5) and p(4) and p(3) and p(2) and p(1) and g(0)) or
		 (p(18) and p(17) and p(16) and p(15) and p(14) and p(13) and p(12) and p(11) and p(10) and p(9) and p(8) and p(7) and p(6) and p(5) and p(4) and p(3) and p(2) and p(1) and p(0) and c(0));

c(20) <= g(19) or
		 (p(19) and g(18)) or
		 (p(19) and p(18) and g(17)) or
		 (p(19) and p(18) and p(17) and g(16)) or
		 (p(19) and p(18) and p(17) and p(16) and g(15)) or
		 (p(19) and p(18) and p(17) and p(16) and p(15) and g(14)) or
		 (p(19) and p(18) and p(17) and p(16) and p(15) and p(14) and g(13)) or
		 (p(19) and p(18) and p(17) and p(16) and p(15) and p(14) and p(13) and g(12)) or
		 (p(19) and p(18) and p(17) and p(16) and p(15) and p(14) and p(13) and p(12) and g(11)) or
		 (p(19) and p(18) and p(17) and p(16) and p(15) and p(14) and p(13) and p(12) and p(11) and g(10)) or
		 (p(19) and p(18) and p(17) and p(16) and p(15) and p(14) and p(13) and p(12) and p(11) and p(10) and g(9)) or
		 (p(19) and p(18) and p(17) and p(16) and p(15) and p(14) and p(13) and p(12) and p(11) and p(10) and p(9) and g(8)) or
		 (p(19) and p(18) and p(17) and p(16) and p(15) and p(14) and p(13) and p(12) and p(11) and p(10) and p(9) and p(8) and g(7)) or
		 (p(19) and p(18) and p(17) and p(16) and p(15) and p(14) and p(13) and p(12) and p(11) and p(10) and p(9) and p(8) and p(7) and g(6)) or
		 (p(19) and p(18) and p(17) and p(16) and p(15) and p(14) and p(13) and p(12) and p(11) and p(10) and p(9) and p(8) and p(7) and p(6) and g(5)) or
		 (p(19) and p(18) and p(17) and p(16) and p(15) and p(14) and p(13) and p(12) and p(11) and p(10) and p(9) and p(8) and p(7) and p(6) and p(5) and g(4)) or
		 (p(19) and p(18) and p(17) and p(16) and p(15) and p(14) and p(13) and p(12) and p(11) and p(10) and p(9) and p(8) and p(7) and p(6) and p(5) and p(4) and g(3)) or
		 (p(19) and p(18) and p(17) and p(16) and p(15) and p(14) and p(13) and p(12) and p(11) and p(10) and p(9) and p(8) and p(7) and p(6) and p(5) and p(4) and p(3) and g(2)) or
		 (p(19) and p(18) and p(17) and p(16) and p(15) and p(14) and p(13) and p(12) and p(11) and p(10) and p(9) and p(8) and p(7) and p(6) and p(5) and p(4) and p(3) and p(2) and g(1)) or
		 (p(19) and p(18) and p(17) and p(16) and p(15) and p(14) and p(13) and p(12) and p(11) and p(10) and p(9) and p(8) and p(7) and p(6) and p(5) and p(4) and p(3) and p(2) and p(1) and g(0)) or
		 (p(19) and p(18) and p(17) and p(16) and p(15) and p(14) and p(13) and p(12) and p(11) and p(10) and p(9) and p(8) and p(7) and p(6) and p(5) and p(4) and p(3) and p(2) and p(1) and p(0) and c(0));

c(21) <= g(20) or
		 (p(20) and g(19)) or
		 (p(20) and p(19) and g(18)) or
		 (p(20) and p(19) and p(18) and g(17)) or
		 (p(20) and p(19) and p(18) and p(17) and g(16)) or
		 (p(20) and p(19) and p(18) and p(17) and p(16) and g(15)) or
		 (p(20) and p(19) and p(18) and p(17) and p(16) and p(15) and g(14)) or
		 (p(20) and p(19) and p(18) and p(17) and p(16) and p(15) and p(14) and g(13)) or
		 (p(20) and p(19) and p(18) and p(17) and p(16) and p(15) and p(14) and p(13) and g(12)) or
		 (p(20) and p(19) and p(18) and p(17) and p(16) and p(15) and p(14) and p(13) and p(12) and g(11)) or
		 (p(20) and p(19) and p(18) and p(17) and p(16) and p(15) and p(14) and p(13) and p(12) and p(11) and g(10)) or
		 (p(20) and p(19) and p(18) and p(17) and p(16) and p(15) and p(14) and p(13) and p(12) and p(11) and p(10) and g(9)) or
		 (p(20) and p(19) and p(18) and p(17) and p(16) and p(15) and p(14) and p(13) and p(12) and p(11) and p(10) and p(9) and g(8)) or
		 (p(20) and p(19) and p(18) and p(17) and p(16) and p(15) and p(14) and p(13) and p(12) and p(11) and p(10) and p(9) and p(8) and g(7)) or
		 (p(20) and p(19) and p(18) and p(17) and p(16) and p(15) and p(14) and p(13) and p(12) and p(11) and p(10) and p(9) and p(8) and p(7) and g(6)) or
		 (p(20) and p(19) and p(18) and p(17) and p(16) and p(15) and p(14) and p(13) and p(12) and p(11) and p(10) and p(9) and p(8) and p(7) and p(6) and g(5)) or
		 (p(20) and p(19) and p(18) and p(17) and p(16) and p(15) and p(14) and p(13) and p(12) and p(11) and p(10) and p(9) and p(8) and p(7) and p(6) and p(5) and g(4)) or
		 (p(20) and p(19) and p(18) and p(17) and p(16) and p(15) and p(14) and p(13) and p(12) and p(11) and p(10) and p(9) and p(8) and p(7) and p(6) and p(5) and p(4) and g(3)) or
		 (p(20) and p(19) and p(18) and p(17) and p(16) and p(15) and p(14) and p(13) and p(12) and p(11) and p(10) and p(9) and p(8) and p(7) and p(6) and p(5) and p(4) and p(3) and g(2)) or
		 (p(20) and p(19) and p(18) and p(17) and p(16) and p(15) and p(14) and p(13) and p(12) and p(11) and p(10) and p(9) and p(8) and p(7) and p(6) and p(5) and p(4) and p(3) and p(2) and g(1)) or
		 (p(20) and p(19) and p(18) and p(17) and p(16) and p(15) and p(14) and p(13) and p(12) and p(11) and p(10) and p(9) and p(8) and p(7) and p(6) and p(5) and p(4) and p(3) and p(2) and p(1) and g(0)) or
		 (p(20) and p(19) and p(18) and p(17) and p(16) and p(15) and p(14) and p(13) and p(12) and p(11) and p(10) and p(9) and p(8) and p(7) and p(6) and p(5) and p(4) and p(3) and p(2) and p(1) and p(0) and c(0));

c(22) <= g(21) or
		 (p(21) and g(20)) or
		 (p(21) and p(20) and g(19)) or
		 (p(21) and p(20) and p(19) and g(18)) or
		 (p(21) and p(20) and p(19) and p(18) and g(17)) or
		 (p(21) and p(20) and p(19) and p(18) and p(17) and g(16)) or
		 (p(21) and p(20) and p(19) and p(18) and p(17) and p(16) and g(15)) or
		 (p(21) and p(20) and p(19) and p(18) and p(17) and p(16) and p(15) and g(14)) or
		 (p(21) and p(20) and p(19) and p(18) and p(17) and p(16) and p(15) and p(14) and g(13)) or
		 (p(21) and p(20) and p(19) and p(18) and p(17) and p(16) and p(15) and p(14) and p(13) and g(12)) or
		 (p(21) and p(20) and p(19) and p(18) and p(17) and p(16) and p(15) and p(14) and p(13) and p(12) and g(11)) or
		 (p(21) and p(20) and p(19) and p(18) and p(17) and p(16) and p(15) and p(14) and p(13) and p(12) and p(11) and g(10)) or
		 (p(21) and p(20) and p(19) and p(18) and p(17) and p(16) and p(15) and p(14) and p(13) and p(12) and p(11) and p(10) and g(9)) or
		 (p(21) and p(20) and p(19) and p(18) and p(17) and p(16) and p(15) and p(14) and p(13) and p(12) and p(11) and p(10) and p(9) and g(8)) or
		 (p(21) and p(20) and p(19) and p(18) and p(17) and p(16) and p(15) and p(14) and p(13) and p(12) and p(11) and p(10) and p(9) and p(8) and g(7)) or
		 (p(21) and p(20) and p(19) and p(18) and p(17) and p(16) and p(15) and p(14) and p(13) and p(12) and p(11) and p(10) and p(9) and p(8) and p(7) and g(6)) or
		 (p(21) and p(20) and p(19) and p(18) and p(17) and p(16) and p(15) and p(14) and p(13) and p(12) and p(11) and p(10) and p(9) and p(8) and p(7) and p(6) and g(5)) or
		 (p(21) and p(20) and p(19) and p(18) and p(17) and p(16) and p(15) and p(14) and p(13) and p(12) and p(11) and p(10) and p(9) and p(8) and p(7) and p(6) and p(5) and g(4)) or
		 (p(21) and p(20) and p(19) and p(18) and p(17) and p(16) and p(15) and p(14) and p(13) and p(12) and p(11) and p(10) and p(9) and p(8) and p(7) and p(6) and p(5) and p(4) and g(3)) or
		 (p(21) and p(20) and p(19) and p(18) and p(17) and p(16) and p(15) and p(14) and p(13) and p(12) and p(11) and p(10) and p(9) and p(8) and p(7) and p(6) and p(5) and p(4) and p(3) and g(2)) or
		 (p(21) and p(20) and p(19) and p(18) and p(17) and p(16) and p(15) and p(14) and p(13) and p(12) and p(11) and p(10) and p(9) and p(8) and p(7) and p(6) and p(5) and p(4) and p(3) and p(2) and g(1)) or
		 (p(21) and p(20) and p(19) and p(18) and p(17) and p(16) and p(15) and p(14) and p(13) and p(12) and p(11) and p(10) and p(9) and p(8) and p(7) and p(6) and p(5) and p(4) and p(3) and p(2) and p(1) and g(0)) or
		 (p(21) and p(20) and p(19) and p(18) and p(17) and p(16) and p(15) and p(14) and p(13) and p(12) and p(11) and p(10) and p(9) and p(8) and p(7) and p(6) and p(5) and p(4) and p(3) and p(2) and p(1) and p(0) and c(0));

c(23) <= g(22) or
		 (p(22) and g(21)) or
		 (p(22) and p(21) and g(20)) or
		 (p(22) and p(21) and p(20) and g(19)) or
		 (p(22) and p(21) and p(20) and p(19) and g(18)) or
		 (p(22) and p(21) and p(20) and p(19) and p(18) and g(17)) or
		 (p(22) and p(21) and p(20) and p(19) and p(18) and p(17) and g(16)) or
		 (p(22) and p(21) and p(20) and p(19) and p(18) and p(17) and p(16) and g(15)) or
		 (p(22) and p(21) and p(20) and p(19) and p(18) and p(17) and p(16) and p(15) and g(14)) or
		 (p(22) and p(21) and p(20) and p(19) and p(18) and p(17) and p(16) and p(15) and p(14) and g(13)) or
		 (p(22) and p(21) and p(20) and p(19) and p(18) and p(17) and p(16) and p(15) and p(14) and p(13) and g(12)) or
		 (p(22) and p(21) and p(20) and p(19) and p(18) and p(17) and p(16) and p(15) and p(14) and p(13) and p(12) and g(11)) or
		 (p(22) and p(21) and p(20) and p(19) and p(18) and p(17) and p(16) and p(15) and p(14) and p(13) and p(12) and p(11) and g(10)) or
		 (p(22) and p(21) and p(20) and p(19) and p(18) and p(17) and p(16) and p(15) and p(14) and p(13) and p(12) and p(11) and p(10) and g(9)) or
		 (p(22) and p(21) and p(20) and p(19) and p(18) and p(17) and p(16) and p(15) and p(14) and p(13) and p(12) and p(11) and p(10) and p(9) and g(8)) or
		 (p(22) and p(21) and p(20) and p(19) and p(18) and p(17) and p(16) and p(15) and p(14) and p(13) and p(12) and p(11) and p(10) and p(9) and p(8) and g(7)) or
		 (p(22) and p(21) and p(20) and p(19) and p(18) and p(17) and p(16) and p(15) and p(14) and p(13) and p(12) and p(11) and p(10) and p(9) and p(8) and p(7) and g(6)) or
		 (p(22) and p(21) and p(20) and p(19) and p(18) and p(17) and p(16) and p(15) and p(14) and p(13) and p(12) and p(11) and p(10) and p(9) and p(8) and p(7) and p(6) and g(5)) or
		 (p(22) and p(21) and p(20) and p(19) and p(18) and p(17) and p(16) and p(15) and p(14) and p(13) and p(12) and p(11) and p(10) and p(9) and p(8) and p(7) and p(6) and p(5) and g(4)) or
		 (p(22) and p(21) and p(20) and p(19) and p(18) and p(17) and p(16) and p(15) and p(14) and p(13) and p(12) and p(11) and p(10) and p(9) and p(8) and p(7) and p(6) and p(5) and p(4) and g(3)) or
		 (p(22) and p(21) and p(20) and p(19) and p(18) and p(17) and p(16) and p(15) and p(14) and p(13) and p(12) and p(11) and p(10) and p(9) and p(8) and p(7) and p(6) and p(5) and p(4) and p(3) and g(2)) or
		 (p(22) and p(21) and p(20) and p(19) and p(18) and p(17) and p(16) and p(15) and p(14) and p(13) and p(12) and p(11) and p(10) and p(9) and p(8) and p(7) and p(6) and p(5) and p(4) and p(3) and p(2) and g(1)) or
		 (p(22) and p(21) and p(20) and p(19) and p(18) and p(17) and p(16) and p(15) and p(14) and p(13) and p(12) and p(11) and p(10) and p(9) and p(8) and p(7) and p(6) and p(5) and p(4) and p(3) and p(2) and p(1) and g(0)) or
		 (p(22) and p(21) and p(20) and p(19) and p(18) and p(17) and p(16) and p(15) and p(14) and p(13) and p(12) and p(11) and p(10) and p(9) and p(8) and p(7) and p(6) and p(5) and p(4) and p(3) and p(2) and p(1) and p(0) and c(0));

	S_o <= p xor c;

END TypeArchitecture;

// VHDL entity ALU, as the project stores it:
--------------------------------------------------------------------------------
-- Project :
-- File    :
-- Autor   :
-- Date    :
--
--------------------------------------------------------------------------------
-- Description :
--
--------------------------------------------------------------------------------

LIBRARY ieee;
USE ieee.std_logic_1164.all;
USE ieee.numeric_std.all;

ENTITY ALU IS
  PORT (
  ------------------------------------------------------------------------------
  --input ports
    input0,input1        : IN  std_logic_vector(31 DOWNTO 0);
    operation		 	: IN std_logic_vector(2 downto 0);
  ------------------------------------------------------------------------------
  --output ports
    zero		: OUT  std_logic;
    saida        		: OUT std_logic_vector(31 DOWNTO 0)
    );
END ALU;

--------------------------------------------------------------------------------
--Complete your VHDL description below
--------------------------------------------------------------------------------

ARCHITECTURE TypeArchitecture OF ALU IS

BEGIN

	process(input0, input1, operation)
	begin
			case operation is
				when "000" =>
					saida <= std_logic_vector(signed(input0) + signed(input1));
	
				when "001" =>
					saida <= std_logic_vector(signed(input0) - signed(input1));
	
				when "100" =>
					saida <= input0 xor input1;
	
				when "110" => 
					saida <= input0 or input1;
	
				when "111" => 
					saida <= input0 and input1;
	
				when others => --apenas zera tudo
					saida <= "00000000000000000000000000000000";

			end case;
	end process;

	zero<='1' when (signed(input0) - signed(input1)=X"000000000000000000000000000000000") else '0';	

END TypeArchitecture;

// VHDL entity datamem, as the project stores it:
library ieee;
use ieee.std_logic_1164.all;
use ieee.std_logic_unsigned.all;

entity datamem is
	port (
		clock : in std_logic;
		write_enable : in std_logic;
		address : in std_logic_vector(15 downto 0);
		input_data : in std_logic_vector(7 downto 0);
		output_data : out std_logic_vector(7 downto 0)
	);
end datamem;
architecture behavioural of datamem is
	type ram_type is array (65536 downto 0) of std_logic_vector (7 downto 0);
	signal RAM : ram_type;
begin
	process (clock, write_enable)
	begin
		if falling_edge(clock) and write_enable = '1' then
			RAM(conv_integer(address)) <= input_data;
		end if;
	end process;
	output_data <= RAM(conv_integer(address));
end behavioural;

// VHDL entity datamem_interface, as the project stores it:
library ieee;
use ieee.std_logic_1164.all;
use ieee.numeric_std.all;
use work.all;

entity datamem_interface is
	port (
		input_data : in std_logic_vector(31 downto 0);
		byte_address : in std_logic_vector(31 downto 0);
		clock, read, write: in std_logic;
		output_data : out std_logic_vector(31 downto 0);
		internal_mem_out0: out std_logic_vector(7 downto 0);
		internal_mem_out1: out std_logic_vector(7 downto 0);
		internal_mem_out2: out std_logic_vector(7 downto 0);
		internal_mem_out3: out std_logic_vector(7 downto 0);
		internal_mem_in0: in std_logic_vector(7 downto 0);
		internal_mem_in1: in std_logic_vector(7 downto 0);
		internal_mem_in2: in std_logic_vector(7 downto 0);
		internal_mem_in3: in std_logic_vector(7 downto 0);
		membank_address_out: out std_logic_vector(15 downto 0)
;
		internal_load_out: out std_logic_vector(3 downto 0)
		);
end entity datamem_interface;

architecture behavioural of datamem_interface is

	signal internal_load : std_logic_vector(3 downto 0);

	signal memory_input_0 : std_logic_vector(7 downto 0);
	signal memory_input_1 : std_logic_vector(7 downto 0);
	signal memory_input_2 : std_logic_vector(7 downto 0);
	signal memory_input_3 : std_logic_vector(7 downto 0);

	signal memory_output_0 : std_logic_vector(7 downto 0);
	signal memory_output_1 : std_logic_vector(7 downto 0);
	signal memory_output_2 : std_logic_vector(7 downto 0);
	signal memory_output_3 : std_logic_vector(7 downto 0);

	signal membank_address : std_logic_vector(31 downto 0);
	signal byte_starting_position : std_logic_vector(1 downto 0) := "00";

begin
	membank_address_acquirement : process (input_data, byte_address, read, write, byte_starting_position, memory_output_0, memory_output_1, memory_output_2, memory_output_3)
	begin
		membank_address <= std_logic_vector(shift_right(unsigned(byte_address), 2)); --Dividing by 4 while throwing away non-integer information
		byte_starting_position <= byte_address(1 downto 0); --Last 2 bits to know if we access the memory or not
		if (write = '1') then --writing to memory, data needs to be split before it gets saved
			if (byte_starting_position = "00") then
				internal_load <= "1111";
				memory_input_3 <= input_data(31 downto 24);
				memory_input_2 <= input_data(23 downto 16);
				memory_input_1 <= input_data(15 downto 8);
				memory_input_0 <= input_data(7 downto 0);
			else
				internal_load <= "0000";
				memory_input_3 <= X"00";
				memory_input_2 <= X"00";
				memory_input_1 <= X"00";
				memory_input_0 <= X"00";
			end if;
		elsif (read = '1') then --reading operation, data needs to be sent to internal registers in the registerfile 
			internal_load <= "0000";
			if (byte_starting_position = "00") then
				output_data <= std_logic_vector(memory_output_3 & memory_output_2 & memory_output_1 & memory_output_0);
			else
				output_data <= X"00000000";
			end if;
		end if;
	end process;

	internal_mem_out0<=memory_input_0;
	internal_mem_out1<=memory_input_1;
	internal_mem_out2<=memory_input_2;
	internal_mem_out3<=memory_input_3;
	memory_output_0<=internal_mem_in0;
	memory_output_1<=internal_mem_in1;
	memory_output_2<=internal_mem_in2;
	memory_output_3<=internal_mem_in3;
	internal_load_out<=internal_load;
	membank_address_out<=membank_address(15 downto 0);

end architecture behavioural;

// VHDL entity register_file, as the project stores it:
library ieee;
use ieee.std_logic_1164.all;
use work.all;

entity register_file is
	port (
write_address : in std_logic_vector(4 downto 0);
		 write_control : in std_logic;
		 load_vector_out : out std_logic_vector(31 downto 0));
end entity register_file;

architecture Behavioral of register_file is

	signal internal_reg_load : std_logic_vector(31 downto 0) := X"00000000";

begin
	register_load_decouple : process (write_address)
	begin
		if (write_control = '1') then
			case write_address is
				when "00000" =>
					internal_reg_load(31 downto 0) <= "00000000000000000000000000000001";
				when "00001" =>
					internal_reg_load(31 downto 0) <= "00000000000000000000000000000010";
				when "00010" =>
					internal_reg_load(31 downto 0) <= "00000000000000000000000000000100";
				when "00011" =>
					internal_reg_load(31 downto 0) <= "00000000000000000000000000001000";
				when "00100" =>
					internal_reg_load(31 downto 0) <= "00000000000000000000000000010000";
				when "00101" =>
					internal_reg_load(31 downto 0) <= "00000000000000000000000000100000";
				when "00110" =>
					internal_reg_load(31 downto 0) <= "00000000000000000000000001000000";
				when "00111" =>
					internal_reg_load(31 downto 0) <= "00000000000000000000000010000000";
				when "01000" =>
					internal_reg_load(31 downto 0) <= "00000000000000000000000100000000";
				when "01001" =>
					internal_reg_load(31 downto 0) <= "00000000000000000000001000000000";
				when "01010" =>
					internal_reg_load(31 downto 0) <= "00000000000000000000010000000000";
				when "01011" =>
					internal_reg_load(31 downto 0) <= "00000000000000000000100000000000";
				when "01100" =>
					internal_reg_load(31 downto 0) <= "00000000000000000001000000000000";
				when "01101" =>
					internal_reg_load(31 downto 0) <= "00000000000000000010000000000000";
				when "01110" =>
					internal_reg_load(31 downto 0) <= "00000000000000000100000000000000";
				when "01111" =>
					internal_reg_load(31 downto 0) <= "00000000000000001000000000000000";
				when "10000" =>
					internal_reg_load(31 downto 0) <= "00000000000000010000000000000000";
				when "10001" =>
					internal_reg_load(31 downto 0) <= "00000000000000100000000000000000";
				when "10010" =>
					internal_reg_load(31 downto 0) <= "00000000000001000000000000000000";
				when "10011" =>
					internal_reg_load(31 downto 0) <= "00000000000010000000000000000000";
				when "10100" =>
					internal_reg_load(31 downto 0) <= "00000000000100000000000000000000";
				when "10101" =>
					internal_reg_load(31 downto 0) <= "00000000001000000000000000000000";
				when "10110" =>
					internal_reg_load(31 downto 0) <= "00000000010000000000000000000000";
				when "10111" =>
					internal_reg_load(31 downto 0) <= "00000000100000000000000000000000";
				when "11000" =>
					internal_reg_load(31 downto 0) <= "00000001000000000000000000000000";
				when "11001" =>
					internal_reg_load(31 downto 0) <= "00000010000000000000000000000000";
				when "11010" =>
					internal_reg_load(31 downto 0) <= "00000100000000000000000000000000";
				when "11011" =>
					internal_reg_load(31 downto 0) <= "00001000000000000000000000000000";
				when "11100" =>
					internal_reg_load(31 downto 0) <= "00010000000000000000000000000000";
				when "11101" =>
					internal_reg_load(31 downto 0) <= "00100000000000000000000000000000";
				when "11110" =>
					internal_reg_load(31 downto 0) <= "01000000000000000000000000000000";
				when "11111" =>
					internal_reg_load(31 downto 0) <= "10000000000000000000000000000000";
				when others =>
					internal_reg_load(31 downto 0) <= "00000000000000000000000000000000";

			end case;
		else
			internal_reg_load(31 downto 0) <= "00000000000000000000000000000000";
		end if;
	end process;

	load_vector_out <= internal_reg_load;
end architecture Behavioral;

// VHDL entity mux_32_1, as the project stores it:
library ieee;
use ieee.std_logic_1164.all;

entity mux_32_1 is
	port (selection : in std_logic_vector(4 downto 0);
		input_0 : in std_logic_vector(31 downto 0);
		input_1 : in std_logic_vector(31 downto 0);
		input_2 : in std_logic_vector(31 downto 0);
		input_3 : in std_logic_vector(31 downto 0);
		input_4 : in std_logic_vector(31 downto 0);
		input_5 : in std_logic_vector(31 downto 0);
		input_6 : in std_logic_vector(31 downto 0);
		input_7 : in std_logic_vector(31 downto 0);
		input_8 : in std_logic_vector(31 downto 0);
		input_9 : in std_logic_vector(31 downto 0);
		input_10 : in std_logic_vector(31 downto 0);
		input_11 : in std_logic_vector(31 downto 0);
		input_12 : in std_logic_vector(31 downto 0);
		input_13 : in std_logic_vector(31 downto 0);
		input_14 : in std_logic_vector(31 downto 0);
		input_15 : in std_logic_vector(31 downto 0);
		input_16 : in std_logic_vector(31 downto 0);
		input_17 : in std_logic_vector(31 downto 0);
		input_18 : in std_logic_vector(31 downto 0);
		input_19 : in std_logic_vector(31 downto 0);
		input_20 : in std_logic_vector(31 downto 0);
		input_21 : in std_logic_vector(31 downto 0);
		input_22 : in std_logic_vector(31 downto 0);
		input_23 : in std_logic_vector(31 downto 0);
		input_24 : in std_logic_vector(31 downto 0);
		input_25 : in std_logic_vector(31 downto 0);
		input_26 : in std_logic_vector(31 downto 0);
		input_27 : in std_logic_vector(31 downto 0);
		input_28 : in std_logic_vector(31 downto 0);
		input_29 : in std_logic_vector(31 downto 0);
		input_30 : in std_logic_vector(31 downto 0);
		input_31 : in std_logic_vector(31 downto 0);
		output_0 : out std_logic_vector(31 downto 0));
end mux_32_1;

architecture behavioral of mux_32_1 is
signal dummy : std_logic_vector(31 downto 0):=x"00000000";
begin
	with selection select
		output_0 <=
		input_0 when "00000",
		input_1 when "00001",
		input_2 when "00010",
		input_3 when "00011",
		input_4 when "00100",
		input_5 when "00101",
		input_6 when "00110",
		input_7 when "00111",
		input_8 when "01000",
		input_9 when "01001",
		input_10 when "01010",
		input_11 when "01011",
		input_12 when "01100",
		input_13 when "01101",
		input_14 when "01110",
		input_15 when "01111",
		input_16 when "10000",
		input_17 when "10001",
		input_18 when "10010",
		input_19 when "10011",
		input_20 when "10100",
		input_21 when "10101",
		input_22 when "10110",
		input_23 when "10111",
		input_24 when "11000",
		input_25 when "11001",
		input_26 when "11010",
		input_27 when "11011",
		input_28 when "11100",
		input_29 when "11101",
		input_30 when "11110",
		input_31 when "11111",
		dummy when others;
end behavioral;

// VHDL entity reg32b_falling_edge, as the project stores it:
library ieee;
use ieee.std_logic_1164.all;

entity reg32b_falling_edge is
	port (reg_in : in std_logic_vector(31 downto 0);
		load : in std_logic;
		clock : in std_logic;
		clear : in std_logic;
		reg_out : out std_logic_vector(31 downto 0));
end reg32b_falling_edge;

architecture description of reg32b_falling_edge is
	signal internal_value : std_logic_vector(31 downto 0) := X"00000000";
begin
	process (clock, clear, load, internal_value)
	begin
		if (clear = '1') then
			internal_value <= X"00000000";
		elsif falling_edge(clock) then
			if (load = '1') then
				internal_value <= reg_in;
			else
				internal_value <= internal_value;
			end if;
		end if;
		reg_out <= internal_value;
	end process;
end description;

// VHDL entity reg32b, as the project stores it:
library ieee;
use ieee.std_logic_1164.all;

entity reg32b is
	port (
		reg_in : in std_logic_vector(31 downto 0);
		load, clock, clear : in std_logic;
		reg_out : out std_logic_vector(31 downto 0)
	);
end reg32b;

architecture description of reg32b is
	signal internal_value : std_logic_vector(31 downto 0) := X"00000000";
begin
	process (clock, clear, load, internal_value)
	begin
		if (clear = '1') then
			internal_value <= X"00000000";
		elsif rising_edge(clock) then
			if (load = '1') then
				internal_value <= reg_in;
			else
				internal_value <= internal_value;
			end if;
		end if;
		reg_out <= internal_value;
	end process;
end description;

// VHDL entity reg1b, as the project stores it:
library ieee;
use ieee.std_logic_1164.all;

entity reg1b is
	port (
		reg_in : in std_logic;
		load, clock, clear : in std_logic;
		reg_out : out std_logic
	);
end reg1b;

architecture description of reg1b is
	signal internal_value : std_logic := '0';
begin
	process (clock, clear, load, internal_value)
	begin
		if (clear = '1') then
			internal_value <= '0';
		elsif rising_edge(clock) then
			if (load = '1') then
				internal_value <= reg_in;
			else
				internal_value <= internal_value;
			end if;
		end if;
		reg_out <= internal_value;
	end process;
end description;

// VHDL entity reg2b, as the project stores it:
library ieee;
use ieee.std_logic_1164.all;

entity reg2b is
	port (
		reg_in : in std_logic_vector(1 downto 0);
		load, clock, clear : in std_logic;
		reg_out : out std_logic_vector(1 downto 0)
	);
end reg2b;

architecture description of reg2b is
	signal internal_value : std_logic_vector(1 downto 0) := "00";
begin
	process (clock, clear, load, internal_value)
	begin
		if (clear = '1') then
			internal_value <= "00";
		elsif rising_edge(clock) then
			if (load = '1') then
				internal_value <= reg_in;
			else
				internal_value <= internal_value;
			end if;
		end if;
		reg_out <= internal_value;
	end process;
end description;

// VHDL entity reg3b, as the project stores it:
library ieee;
use ieee.std_logic_1164.all;

entity reg3b is
	port (
		reg_in : in std_logic_vector(2 downto 0);
		load, clock, clear : in std_logic;
		reg_out : out std_logic_vector(2 downto 0)
	);
end reg3b;

architecture description of reg3b is
	signal internal_value : std_logic_vector(2 downto 0) := "000";
begin
	process (clock, clear, load, internal_value)
	begin
		if (clear = '1') then
			internal_value <= "000";
		elsif rising_edge(clock) then
			if (load = '1') then
				internal_value <= reg_in;
			else
				internal_value <= internal_value;
			end if;
		end if;
		reg_out <= internal_value;
	end process;
end description;

// VHDL entity reg4b, as the project stores it:
library ieee;
use ieee.std_logic_1164.all;

entity reg4b is
	port (
		reg_in : in std_logic_vector(3 downto 0);
		load, clock, clear : in std_logic;
		reg_out : out std_logic_vector(3 downto 0)
	);
end reg4b;

architecture description of reg4b is
	signal internal_value : std_logic_vector(3 downto 0) := "0000";
begin
	process (clock, clear, load, internal_value)
	begin
		if (clear = '1') then
			internal_value <= "0000";
		elsif rising_edge(clock) then
			if (load = '1') then
				internal_value <= reg_in;
			else
				internal_value <= internal_value;
			end if;
		end if;
		reg_out <= internal_value;
	end process;
end description;

// VHDL entity reg5b, as the project stores it:
library ieee;
use ieee.std_logic_1164.all;

entity reg5b is
	port (
		reg_in : in std_logic_vector(4 downto 0);
		load, clock, clear : in std_logic;
		reg_out : out std_logic_vector(4 downto 0)
	);
end reg5b;

architecture description of reg5b is
	signal internal_value : std_logic_vector(4 downto 0) := "00000";
begin
	process (clock, clear, load, internal_value)
	begin
		if (clear = '1') then
			internal_value <= "00000";
		elsif rising_edge(clock) then
			if (load = '1') then
				internal_value <= reg_in;
			else
				internal_value <= internal_value;
			end if;
		end if;
		reg_out <= internal_value;
	end process;
end description;

// VHDL entity mux_2_1, as the project stores it:
library ieee;
use ieee.std_logic_1164.all;

entity mux_2_1 is
	port (
		selection : in std_logic;
		input_0, input_1 : in std_logic_vector(31 downto 0);
		output_0 : out std_logic_vector(31 downto 0)
	);
end mux_2_1;

architecture behavioral of mux_2_1 is
begin
	with selection select
		output_0 <=
		input_0 when '0',
		input_1 when '1',
		"XXXXXXXXXXXXXXXXXXXXXXXXXXXXXXXX" when others;
end behavioral;

// VHDL entity reg24b, as the project stores it:
library ieee;
use ieee.std_logic_1164.all;

entity reg24b is
	port (
		reg_in : in std_logic_vector(23 downto 0);
		load, clock, clear : in std_logic;
		reg_out : out std_logic_vector(23 downto 0)
	);
end reg24b;

architecture description of reg24b is
	signal internal_value : std_logic_vector(23 downto 0) := X"000000";
begin
	process (clock, clear, load, internal_value)
	begin
		if (clear = '1') then
			internal_value <= X"000000";
		elsif rising_edge(clock) then
			if (load = '1') then
				internal_value <= reg_in;
			else
				internal_value <= internal_value;
			end if;
		end if;
		reg_out <= internal_value;
	end process;
end description;

// VHDL entity mux_2_1_24b, as the project stores it:
library ieee;
use ieee.std_logic_1164.all;

entity mux_2_1_24b is
	port (
		selection : in std_logic;
		input_0, input_1 : in std_logic_vector(23 downto 0);
		output_0 : out std_logic_vector(23 downto 0)
	);
end mux_2_1_24b;

architecture behavioral of mux_2_1_24b is
begin
	with selection select
		output_0 <=
		input_0 when '0',
		input_1 when '1',
		"XXXXXXXXXXXXXXXXXXXXXXXX" when others;
end behavioral;
